# Fritzing sketch CloseLoop_ServoStepper_Motor_SetUp (saved by Fritzing 1.0.5)
breadboards: 1

parts:
  Componente1 = Arduino Uno (Rev3)
  T1 = T60 Stepper Motor Driver [part_number=T60]
  A1 = Drok Power Supply 200570 [part_number=S-350-60 package=THT]
  M1 = Stepper Motor - 57A3ED Rtelligent [part_number=57A3ED]

nets:
  N1: Componente1.D9_PWM, T1.ENA-, T1.DIR+, T1.PUL+
  N2: Componente1.GND, T1.ENA+, T1.DIR-, T1.PUL-
  N3: T1.B-, M1.B-
  N4: T1.B+, M1.B+
  N5: T1.A-, M1.A-
  N6: T1.A+, M1.A+
  N7: T1.V+, A1.+V1, A1.+V3
  N8: T1.V-, A1.-V1, A1.-V3
  N9: T1.EB+, M1.EB+
  N10: T1.EB-, M1.EB-
  N11: T1.EA+, M1.EA+
  N12: T1.EA-, M1.EA-
  VCC: T1.VCC, M1.VCC
  GND: T1.GND, M1.GND

custom parts:
  T60 Stepper Motor Driver: Stepper servo is a stepper motor scheme formed based on the common open loop stepper motor in combination with position feedback and servo algorithm, which features high speed, high torque, high precision, low vibration, low heating and no loss of step. Based on TI's new 32-bit DSP processing chip platform, T series stepper servo driver uses the field oriented control (FOC) and vector field-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
  Drok Power Supply 200570: 480W power supply. variable voltge
  Stepper Motor - 57A3ED Rtelligent: New 2-phase closed loop stepper motors AM seriesare based on Cz optimized magnetic circuit design and the latest compact M-shaped molds. The motor body uses high magnetic density stator and rotor materials with high energy efficiency.
