# Fritzing sketch LoadCell_1kg_SetUp (saved by Fritzing 1.0.5)
breadboards: 1

parts:
  Componente1 = Arduino Nano (Rev3.0)
  C1 = Ceramic Capacitor [capacitance=100nF voltage=35V package="100 mil [THT, multilayer]"]
  C2 = Electrolytic Capacitor [capacitance=10µF voltage=35V package="100 mil [THT, electrolytic]"]
  R1 = Resistor [tolerance=±5% power=0.25W resistance=10k package=THT]
  J1 = Generic female header - 2 pins [form="♀ (female)" package=THT]
  A3 = DYLY106 load cell Stype [package=THT]
  A4 = Drok Power Supply 200570 [part_number=S-350-60 package=THT]

nets:
  N1: Componente1.GND, C1.0, J1.O-
  N2: Componente1.A0, C2.+, R1.Pin_0
  N3: C1.1, C2.-
  N4: R1.Pin_1, J1.O+
  N5: J1.V-, A4.-V1, A4.-V3
  N6: J1.V+, A4.+V1, A4.+V3
  N7: J1.S+, A3.S+
  N8: J1.S-, A3.S-
  N9: J1.E+, A3.E+
  N10: J1.E-, A3.E-

notes:
  24 V power supply

custom parts:
  Generic female header - 2 pins: Generic female header
  DYLY106 load cell Stype: DYLY-106 High accuracy miniature tension load cell Weighing Scale 500g 1kg 5kg 10kg 20kg 30kg 50kg super micro S type load cell
  Drok Power Supply 200570: 480W power supply. variable voltge
