# Fritzing sketch LoadCell_50kg_SetUp (saved by Fritzing 1.0.5)
breadboards: 1

parts:
  Componente1 = Arduino Nano (Rev3.0)
  A4 = Drok Power Supply 200570 [part_number=S-350-60 package=THT]
  PART1 = Load Cell Amplifier - WXD-D70(JY-S60) [part_number=" WXD-D70 - JY-S60"]
  A5 = DYLY106 load cell Stype [package=THT]

nets:
  GND: Componente1.GND, A4.-V3, PART1.GND
  N1: Componente1.A0, PART1.Vo
  N2: A4.+V3, PART1.VCC
  N3: PART1.RED, A5.E+
  N4: PART1.BLK, A5.E-
  N5: PART1.WHT, A5.S+
  N6: PART1.GRN, A5.S-
  N7: PART1.YLW, A5.Shield

notes:
  24 V power supply

custom parts:
  Drok Power Supply 200570: 480W power supply. variable voltge
  Load Cell Amplifier - WXD-D70(JY-S60): Load Cell Amplifier is a breakout board that allows you to easily read load cells to measure weight. By connecting the amplifier to your microcontroller you will be able to read the changes in the resistance of the load cell and with some calibration you’ll be able to get very accurate weight measurements. This can be handy for creating your own industrial scale, process control, or simple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
  DYLY106 load cell Stype: DYLY-106 High accuracy miniature tension load cell Weighing Scale 500g 1kg 5kg 10kg 20kg 30kg 50kg super micro S type load cell
